# Fritzing sketch Untitled Sketch 2 (saved by Fritzing 1.0.2b)
breadboards: 1

parts:
  LED1 = smd LED [color="Red (633nm)" package="1206 [SMD]"]
  LED2 = smd LED [color="Red (633nm)" package="1206 [SMD]"]
  LED3 = smd LED [color="Red (633nm)" package="1206 [SMD]"]
  LED4 = smd LED [color="Red (633nm)" package="1206 [SMD]"]
  R1 = Resistor [tolerance=±5% power=0.25W resistance=220 package=THT]
  R2 = Resistor [tolerance=±5% power=0.25W resistance=220 package=THT]
  R3 = Resistor [tolerance=±5% power=0.25W resistance=220 package=THT]
  R4 = Resistor [tolerance=±5% power=0.25W resistance=220 package=THT]
  Part1 = Arduino Uno (Rev3)

nets:
  N1: LED1.cathode, R1.Pin_1
  N2: LED1.anode, Part1.D11_PWM/MOSI
  N3: LED2.cathode, R2.Pin_1
  N4: LED2.anode, Part1.D10_PWM/SS
  N5: LED3.cathode, R3.Pin_1
  N6: LED3.anode, Part1.D9_PWM
  N7: LED4.cathode, R4.Pin_1
  N8: LED4.anode, Part1.D6_PWM
  N9: R1.Pin_0, R2.Pin_0, R3.Pin_0, R4.Pin_0, Part1.GND
